# Fritzing sketch picosetup (saved by Fritzing 1.0.4)
breadboards: 2

parts:
  R1 = TRIMPOT [maximum_resistance=10kΩ knob_status=50% power=0.5W package=3362u-2]
  S1 = Momentary Switch [package=ksa_sealed_tac_switch]
  S2 = Momentary Switch [package=ksa_sealed_tac_switch]
  J1 = Piezo Speaker
  U1 = 7-SEGMENT-DISPLAY-1_-RED [package=7-segment-1_pth]  # not connected
  Pico/Pico2_Mod_1 = Raspberry Pi Pico or Pico 2
  Pico/Pico2_Mod_2 = Raspberry Pi Pico or Pico 2
  U2 = MOC3031-M [package=dil06]
  U3 = MOC3031-M [package=dil06]
  U4 = MOC3031-M [package=dil06]
  U5 = MOC3031-M [package=dil06]
  LED1 = Super Flux RGB LED (com. anode)

nets:
  N1: R1.CCW, Pico/Pico2_Mod_1.pin_3, Pico/Pico2_Mod_1.pin_8, Pico/Pico2_Mod_1.pin_13, Pico/Pico2_Mod_1.pin_18, Pico/Pico2_Mod_1.pin_23, Pico/Pico2_Mod_1.pin_28, Pico/Pico2_Mod_1.pin_33, Pico/Pico2_Mod_1.pin_38
  N2: R1.WIPER, Pico/Pico2_Mod_1.pin_31
  N3: R1.CW, Pico/Pico2_Mod_1.pin_36
  N4: S1.1, S2.1
  N5: S1.3, Pico/Pico2_Mod_1.pin_22
  N6: S2.3, Pico/Pico2_Mod_1.pin_21
  N7: J1.pin2, Pico/Pico2_Mod_1.pin_20
  N8: Pico/Pico2_Mod_1.pin_15, LED1.red_cathode
  N9: Pico/Pico2_Mod_1.pin_17, LED1.green_cathode
  N10: Pico/Pico2_Mod_2.pin_3, Pico/Pico2_Mod_2.pin_8, Pico/Pico2_Mod_2.pin_13, Pico/Pico2_Mod_2.pin_18, Pico/Pico2_Mod_2.pin_23, Pico/Pico2_Mod_2.pin_28, Pico/Pico2_Mod_2.pin_33, Pico/Pico2_Mod_2.pin_38
  N11: U2.1, U5.2
  N12: U3.2, U4.1

custom parts:
  Raspberry Pi Pico or Pico 2: Raspberry Pi Pico and Pico 2. Based around the RP2040 and RP2350 microcontrollers respectively, Picos are low cost microcontroller device bringing Raspberry Pi quality, cost, and easy of use to the microcontroller space. Jan 2021, Split part in to two versions: tht (this one) and SMD. This one will drill holes for a .1 in header in pcb to allow plugging in the module as well as providing pads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
